// Logisim project csm.circ as structural Verilog: 1 circuit, main circuit main
module main (
  input  Y0,
  input  Y1,
  input  Y2,
  input  Y3,
  input  ZERO,
  input  X0,
  input  X1,
  input  X2,
  input  X3,
  output P0,
  output P1,
  output P2,
  output P3,
  output P4,
  output P5,
  output P6,
  output P7,
  output out_18
);

  wire adder_1_cout, adder_2_cout, adder_2_out, adder_3_cout, adder_4_cout, adder_4_out, adder_5_cout,
       adder_5_out, adder_6_cout, adder_7_cout, adder_7_out, adder_8_cout, adder_8_out, adder_9_cout,
       adder_9_out, adder_10_cout, adder_11_cout, adder_11_out, adder_12_cout, adder_12_out, adder_13_cout,
       adder_13_out, adder_14_cout, adder_15_cout, adder_15_out, adder_16_cout, adder_16_out, adder_17_cout,
       adder_18_cout, adder_18_out, adder_19_cout, and_1_out, and_2_out, and_3_out, and_4_out, and_5_out,
       and_6_out, and_7_out, and_8_out, and_9_out, and_10_out, and_11_out, and_12_out;

  Adder #(.width(1)) adder_1 (.a(X0), .b(Y0), .out(P0), .cin(X3), .cout(adder_1_cout));
  and and_1 (and_1_out, X1, Y0);
  Adder #(.width(1)) adder_2 (.a(X0), .b(Y1), .out(adder_2_out), .cin(X3), .cout(adder_2_cout));
  Adder #(.width(1)) adder_3 (.a(and_1_out), .b(adder_2_out), .out(P1), .cin(adder_1_cout), .cout(adder_3_cout));
  and and_2 (and_2_out, X1, Y1);
  and and_3 (and_3_out, X2, Y0);
  Adder #(.width(1)) adder_4 (.a(X0), .b(Y2), .out(adder_4_out), .cin(X3), .cout(adder_4_cout));
  Adder #(.width(1)) adder_5 (
    .a(and_2_out), .b(adder_4_out), .out(adder_5_out), .cin(adder_2_cout), .cout(adder_5_cout));
  Adder #(.width(1)) adder_6 (.a(and_3_out), .b(adder_5_out), .out(P2), .cin(adder_3_cout), .cout(adder_6_cout));
  and and_4 (and_4_out, X1, Y2);
  and and_5 (and_5_out, X2, Y1);
  Adder #(.width(1)) adder_7 (.a(X0), .b(Y3), .out(adder_7_out), .cin(X3), .cout(adder_7_cout));
  Adder #(.width(1)) adder_8 (
    .a(and_5_out), .b(adder_9_out), .out(adder_8_out), .cin(adder_5_cout), .cout(adder_8_cout));
  and and_6 (and_6_out, X3, Y0);
  Adder #(.width(1)) adder_9 (
    .a(and_4_out), .b(adder_7_out), .out(adder_9_out), .cin(adder_4_cout), .cout(adder_9_cout));
  Adder #(.width(1)) adder_10 (.a(and_6_out), .b(adder_8_out), .out(P3), .cin(adder_6_cout), .cout(adder_10_cout));
  and and_7 (and_7_out, X1, Y3);
  and and_8 (and_8_out, X2, Y2);
  and and_9 (and_9_out, X3, Y1);
  Adder #(.width(1)) adder_11 (.a(and_7_out), .b(X3), .out(adder_11_out), .cin(adder_7_cout), .cout(adder_11_cout));
  Adder #(.width(1)) adder_12 (
    .a(and_8_out), .b(adder_11_out), .out(adder_12_out), .cin(adder_9_cout), .cout(adder_12_cout));
  Adder #(.width(1)) adder_13 (
    .a(and_9_out), .b(adder_12_out), .out(adder_13_out), .cin(adder_8_cout), .cout(adder_13_cout));
  Adder #(.width(1)) adder_14 (.a(X3), .b(adder_13_out), .out(P4), .cin(adder_10_cout), .cout(adder_14_cout));
  and and_10 (and_10_out, X2, Y3);
  and and_11 (and_11_out, X3, Y2);
  Adder #(.width(1)) adder_15 (.a(and_10_out), .b(X3), .out(adder_15_out), .cin(adder_11_cout), .cout(adder_15_cout));
  Adder #(.width(1)) adder_16 (
    .a(and_11_out), .b(adder_15_out), .out(adder_16_out), .cin(adder_12_cout), .cout(adder_16_cout));
  Adder #(.width(1)) adder_17 (
    .a(adder_14_cout), .b(adder_16_out), .out(P5), .cin(adder_13_cout), .cout(adder_17_cout));
  and and_12 (and_12_out, X3, Y3);
  Adder #(.width(1)) adder_18 (.a(and_12_out), .b(X3), .out(adder_18_out), .cin(adder_15_cout), .cout(adder_18_cout));
  Adder #(.width(1)) adder_19 (
    .a(adder_17_cout), .b(adder_18_out), .out(P6), .cin(adder_16_cout), .cout(adder_19_cout));
  Adder #(.width(1)) adder_20 (.a(adder_19_cout), .b(X3), .out(out_18), .cin(adder_18_cout), .cout(P7));

  assign ZERO = X3;
endmodule
